// Logisim project CPUE.circ as structural Verilog: 1 circuit, main circuit main
module main (
  input  MODE,
  input  H_MODE,
  input  MHA,
  input  in_4,
  input  in_5,
  input  in_6,
  input  RESET,
  input  MODE_2,
  input  in_9,
  input  A_CLEAR,
  input  in_11,
  input  in_12,
  input  in_13,
  input  B_CLEAR,
  input  O_CLEAR,
  input  IR_CLEAR,
  input  in_17,
  input  RSC,
  input  FR,
  input  FI,
  output out_21,
  output out_22,
  output out_23,
  output out_24,
  output out_25,
  output out_26,
  output out_27,
  output out_28
);

  wire adder_1_cout, adder_1_out, adder_2_cout, adder_2_out, adder_3_cout, adder_3_out, adder_4_cout,
       adder_4_out, adder_5_cout, adder_5_out, adder_6_cout, adder_6_out, adder_7_cout, adder_7_out,
       adder_8_cout, adder_8_out, and_1_out, and_2_out, and_3_out, and_4_out, and_5_out, and_6_out,
       and_7_out, and_8_out, and_9_out, and_10_out, and_11_out, and_12_out, and_13_out, and_14_out,
       and_15_out, and_16_out, button_1_out, CPU_CLOCK_out, d_ff_1_q, d_ff_2_q, d_ff_4_q, d_ff_5_q, d_ff_6_q,
       d_ff_7_q, d_ff_9_q, d_ff_10_q, d_ff_11_q, d_ff_12_q, d_ff_13_q, d_ff_15_q, d_ff_16_q, d_ff_17_q,
       d_ff_20_q, d_ff_21_q, d_ff_22_q, d_ff_23_q, d_ff_25_q, d_ff_26_q, d_ff_27_q, d_ff_28_q, d_ff_31_q,
       d_ff_32_q, d_ff_34_q, d_ff_35_q, d_ff_37_q, d_ff_38_q, d_ff_40_q, d_ff_41_q, d_ff_43_q, d_ff_44_q,
       d_ff_46_q, d_ff_47_q, demultiplexer_1_out0, demultiplexer_1_out1, demultiplexer_1_out2,
       demultiplexer_1_out3, demultiplexer_1_out4, demultiplexer_1_out5, demultiplexer_1_out6,
       demultiplexer_1_out7, demultiplexer_1_out8, demultiplexer_1_out9, demultiplexer_1_out10,
       demultiplexer_1_out11, demultiplexer_1_out12, demultiplexer_1_out13, demultiplexer_1_out14,
       demultiplexer_1_out15, dipswitch_2_sw1, dipswitch_2_sw2, dipswitch_2_sw3, dipswitch_2_sw4,
       dipswitch_2_sw5, dipswitch_2_sw6, dipswitch_2_sw7, dipswitch_2_sw8, j_k_ff_1_qn, j_k_ff_2_qn,
       j_k_ff_3_qn, j_k_ff_5_q, j_k_ff_5_qn, j_k_ff_6_q, j_k_ff_6_qn, j_k_ff_7_q, j_k_ff_7_qn, j_k_ff_8_q,
       j_k_ff_8_qn, j_k_ff_9_q, j_k_ff_9_qn, j_k_ff_10_q, j_k_ff_10_qn, j_k_ff_11_q, j_k_ff_11_qn,
       j_k_ff_12_q, MANUAL_out, multiplexer_4_out, multiplexer_5_out, multiplexer_11_out, nor_1_out,
       not_1_out, not_2_out, not_3_out, undriven, undriven_2, undriven_3, undriven_4, xor_1_out, xor_2_out,
       xor_3_out, xor_4_out, xor_5_out, xor_6_out, xor_7_out, xor_8_out;
  wire [4:0] controlled_buffer_9_out;
  wire [7:0] d_ff_45_q, multiplexer_10_out, rom_2_data, rom_3_data, rom_4_data;
  wire [8:0] j_k_ff_1_q;
  wire [12:0] dipswitch_1_sw13, ram_1_dout;
  wire [16:0] rom_1_data;

  D_Flip_Flop d_ff_1 (.D(out_24), .clk(and_3_out), .Q(d_ff_1_q), .preset(in_6), .reset(RESET));  // open: Qn
  D_Flip_Flop d_ff_2 (.D(out_23), .clk(and_3_out), .Q(d_ff_2_q), .preset(in_6), .reset(RESET));  // open: Qn
  Multiplexer multiplexer_1 (.in0(d_ff_13_q), .in1(dipswitch_2_sw1), .out(multiplexer_10_out[7]), .sel(MODE_2));
  LED led_1 (.in(multiplexer_10_out[7]));
  and and_1 (and_1_out, and_2_out, rom_1_data[14]);
  D_Flip_Flop d_ff_3 (
    .D(controlled_buffer_9_out[4]), .clk(and_1_out), .Q(j_k_ff_1_q[8]), .preset(undriven), .reset(IR_CLEAR));  // open: Qn
  D_Flip_Flop d_ff_4 (.D(out_24), .clk(and_1_out), .Q(d_ff_4_q), .preset(undriven_3), .reset(IR_CLEAR));  // open: Qn
  D_Flip_Flop d_ff_5 (.D(out_23), .clk(and_1_out), .Q(d_ff_5_q), .preset(undriven_2), .reset(IR_CLEAR));  // open: Qn
  J_K_Flip_Flop j_k_ff_1 (
    .J(in_17), .K(in_17), .clk(not_3_out), .Q(j_k_ff_1_q[0]), .Qn(j_k_ff_1_qn), .reset(rom_1_data[1]));  // open: preset
  LED led_2 (.in(demultiplexer_1_out0));
  LED led_3 (.in(demultiplexer_1_out1));
  Clock CPU_CLOCK (.out(CPU_CLOCK_out));
  Button MANUAL (.out(MANUAL_out));
  not not_1 (not_1_out, rom_1_data[4]);
  D_Flip_Flop d_ff_6 (.D(out_25), .clk(and_3_out), .Q(d_ff_6_q), .preset(in_6), .reset(RESET));  // open: Qn
  D_Flip_Flop d_ff_7 (.D(out_22), .clk(and_3_out), .Q(d_ff_7_q), .preset(in_6), .reset(RESET));  // open: Qn
  Multiplexer multiplexer_2 (.in0(d_ff_2_q), .in1(dipswitch_2_sw3), .out(multiplexer_10_out[5]), .sel(MODE_2));
  Multiplexer multiplexer_3 (.in0(d_ff_7_q), .in1(dipswitch_2_sw2), .out(multiplexer_10_out[6]), .sel(MODE_2));
  LED led_4 (.in(multiplexer_10_out[5]));
  LED led_5 (.in(multiplexer_10_out[4]));
  LED led_6 (.in(multiplexer_10_out[3]));
  LED led_7 (.in(multiplexer_10_out[6]));
  RAM #(.dataWidth(13)) ram_1 (
    .addr(multiplexer_10_out), .we(in_11), .oe(in_12), .clk(and_2_out), .din(dipswitch_1_sw13),
    .dout(ram_1_dout));
  DipSwitch #(.number(13)) dipswitch_1 (
    .sw1(dipswitch_1_sw13[12]), .sw2(dipswitch_1_sw13[11]), .sw3(dipswitch_1_sw13[10]),
    .sw4(dipswitch_1_sw13[9]), .sw5(dipswitch_1_sw13[8]), .sw6(dipswitch_1_sw13[7]),
    .sw7(dipswitch_1_sw13[6]), .sw8(dipswitch_1_sw13[5]), .sw9(dipswitch_1_sw13[4]),
    .sw10(dipswitch_1_sw13[3]), .sw11(dipswitch_1_sw13[2]), .sw12(dipswitch_1_sw13[1]),
    .sw13(dipswitch_1_sw13[0]));
  LED led_8 (.in(ram_1_dout[11]));
  LED led_9 (.in(ram_1_dout[10]));
  LED led_10 (.in(ram_1_dout[9]));
  LED led_11 (.in(ram_1_dout[12]));
  D_Flip_Flop d_ff_8 (
    .D(controlled_buffer_9_out[3]), .clk(and_1_out), .Q(j_k_ff_1_q[7]), .preset(undriven), .reset(IR_CLEAR));  // open: Qn
  D_Flip_Flop d_ff_9 (.D(out_25), .clk(and_1_out), .Q(d_ff_9_q), .preset(undriven_3), .reset(IR_CLEAR));  // open: Qn
  D_Flip_Flop d_ff_10 (.D(out_22), .clk(and_1_out), .Q(d_ff_10_q), .preset(undriven_2), .reset(IR_CLEAR));  // open: Qn
  LED led_12 (.in(j_k_ff_1_q[7]));
  LED led_13 (.in(j_k_ff_1_q[6]));
  LED led_14 (.in(j_k_ff_1_q[5]));
  LED led_15 (.in(j_k_ff_1_q[8]));
  J_K_Flip_Flop j_k_ff_2 (
    .J(in_17), .K(in_17), .clk(j_k_ff_1_qn), .Q(j_k_ff_1_q[1]), .Qn(j_k_ff_2_qn), .reset(rom_1_data[1]));  // open: preset
  LED led_16 (.in(demultiplexer_1_out3));
  LED led_17 (.in(demultiplexer_1_out4));
  LED led_18 (.in(demultiplexer_1_out5));
  LED led_19 (.in(demultiplexer_1_out2));
  ROM #(.addrWidth(9), .dataWidth(17)) rom_1 (.addr(j_k_ff_1_q), .data(rom_1_data));
  Multiplexer multiplexer_4 (.in0(CPU_CLOCK_out), .in1(MANUAL_out), .out(multiplexer_4_out), .sel(MODE));
  Multiplexer multiplexer_5 (.in0(not_1_out), .in1(not_2_out), .out(multiplexer_5_out), .sel(H_MODE));
  not not_2 (not_2_out, MHA);
  D_Flip_Flop d_ff_11 (.D(out_26), .clk(and_3_out), .Q(d_ff_11_q), .preset(in_6), .reset(RESET));  // open: Qn
  D_Flip_Flop d_ff_12 (.D(out_27), .clk(and_3_out), .Q(d_ff_12_q), .preset(in_6), .reset(RESET));  // open: Qn
  D_Flip_Flop d_ff_13 (.D(out_21), .clk(and_3_out), .Q(d_ff_13_q), .preset(in_6), .reset(RESET));  // open: Qn
  Multiplexer multiplexer_6 (.in0(d_ff_1_q), .in1(dipswitch_2_sw4), .out(multiplexer_10_out[4]), .sel(MODE_2));
  Multiplexer multiplexer_7 (.in0(d_ff_6_q), .in1(dipswitch_2_sw5), .out(multiplexer_10_out[3]), .sel(MODE_2));
  LED led_20 (.in(multiplexer_10_out[2]));
  LED led_21 (.in(multiplexer_10_out[1]));
  LED led_22 (.in(multiplexer_10_out[0]));
  LED led_23 (.in(ram_1_dout[8]));
  LED led_24 (.in(ram_1_dout[7]));
  LED led_25 (.in(ram_1_dout[6]));
  LED led_26 (.in(ram_1_dout[5]));
  LED led_27 (.in(controlled_buffer_9_out[4]));
  D_Flip_Flop d_ff_14 (
    .D(controlled_buffer_9_out[2]), .clk(and_1_out), .Q(j_k_ff_1_q[6]), .preset(undriven), .reset(IR_CLEAR));  // open: Qn
  D_Flip_Flop d_ff_15 (.D(out_26), .clk(and_1_out), .Q(d_ff_15_q), .preset(undriven_3), .reset(IR_CLEAR));  // open: Qn
  D_Flip_Flop d_ff_16 (.D(out_21), .clk(and_1_out), .Q(d_ff_16_q), .preset(undriven_2), .reset(IR_CLEAR));  // open: Qn
  LED led_28 (.in(j_k_ff_1_q[4]));
  LED led_29 (.in(d_ff_16_q));
  LED led_30 (.in(d_ff_10_q));
  LED led_31 (.in(d_ff_5_q));
  J_K_Flip_Flop j_k_ff_3 (
    .J(in_17), .K(in_17), .clk(j_k_ff_2_qn), .Q(j_k_ff_1_q[2]), .Qn(j_k_ff_3_qn), .reset(rom_1_data[1]));  // open: preset
  Demultiplexer #(.select(4)) demultiplexer_1 (
    .out0(demultiplexer_1_out0), .out1(demultiplexer_1_out1), .out2(demultiplexer_1_out2),
    .out3(demultiplexer_1_out3), .out4(demultiplexer_1_out4), .out5(demultiplexer_1_out5),
    .out6(demultiplexer_1_out6), .out7(demultiplexer_1_out7), .out8(demultiplexer_1_out8),
    .out9(demultiplexer_1_out9), .out10(demultiplexer_1_out10), .out11(demultiplexer_1_out11),
    .out12(demultiplexer_1_out12), .out13(demultiplexer_1_out13), .out14(demultiplexer_1_out14),
    .out15(demultiplexer_1_out15), .in(RSC), .sel(j_k_ff_1_q[3:0]));
  LED led_32 (.in(demultiplexer_1_out6));
  LED led_33 (.in(demultiplexer_1_out7));
  LED led_34 (.in(demultiplexer_1_out8));
  LED led_35 (.in(demultiplexer_1_out9));
  and and_2 (and_2_out, multiplexer_4_out, multiplexer_5_out);
  LED led_36 (.in(and_2_out));
  and and_3 (and_3_out, and_2_out, rom_1_data[16]);
  D_Flip_Flop d_ff_17 (.D(out_28), .clk(and_3_out), .Q(d_ff_17_q), .preset(in_6), .reset(RESET));  // open: Qn
  Multiplexer multiplexer_8 (.in0(d_ff_11_q), .in1(dipswitch_2_sw6), .out(multiplexer_10_out[2]), .sel(MODE_2));
  Multiplexer multiplexer_9 (.in0(d_ff_12_q), .in1(dipswitch_2_sw7), .out(multiplexer_10_out[1]), .sel(MODE_2));
  DipSwitch dipswitch_2 (
    .sw1(dipswitch_2_sw1), .sw2(dipswitch_2_sw2), .sw3(dipswitch_2_sw3), .sw4(dipswitch_2_sw4),
    .sw5(dipswitch_2_sw5), .sw6(dipswitch_2_sw6), .sw7(dipswitch_2_sw7), .sw8(dipswitch_2_sw8));
  LED led_37 (.in(ram_1_dout[4]));
  LED led_38 (.in(ram_1_dout[3]));
  LED led_39 (.in(ram_1_dout[2]));
  LED led_40 (.in(ram_1_dout[1]));
  LED led_41 (.in(controlled_buffer_9_out[3]));
  LED led_42 (.in(controlled_buffer_9_out[2]));
  LED led_43 (.in(controlled_buffer_9_out[1]));
  LED led_44 (.in(controlled_buffer_9_out[0]));
  D_Flip_Flop d_ff_18 (
    .D(controlled_buffer_9_out[1]), .clk(and_1_out), .Q(j_k_ff_1_q[5]), .preset(undriven), .reset(IR_CLEAR));  // open: Qn
  D_Flip_Flop d_ff_19 (
    .D(controlled_buffer_9_out[0]), .clk(and_1_out), .Q(j_k_ff_1_q[4]), .preset(undriven), .reset(IR_CLEAR));  // open: Qn
  D_Flip_Flop d_ff_20 (.D(out_27), .clk(and_1_out), .Q(d_ff_20_q), .preset(undriven_3), .reset(IR_CLEAR));  // open: Qn
  D_Flip_Flop d_ff_21 (.D(out_28), .clk(and_1_out), .Q(d_ff_21_q), .preset(undriven_3), .reset(IR_CLEAR));  // open: Qn
  LED led_45 (.in(d_ff_4_q));
  LED led_46 (.in(d_ff_9_q));
  LED led_47 (.in(d_ff_15_q));
  LED led_48 (.in(d_ff_20_q));
  J_K_Flip_Flop j_k_ff_4 (
    .J(in_17), .K(in_17), .clk(j_k_ff_3_qn), .Q(j_k_ff_1_q[3]), .reset(rom_1_data[1]));  // open: Qn, preset
  LED led_49 (.in(demultiplexer_1_out10));
  LED led_50 (.in(demultiplexer_1_out11));
  LED led_51 (.in(demultiplexer_1_out12));
  LED led_52 (.in(demultiplexer_1_out13));
  Multiplexer multiplexer_10 (.in0(d_ff_17_q), .in1(dipswitch_2_sw8), .out(multiplexer_10_out[0]), .sel(MODE_2));
  assign out_28 = rom_1_data[15] ? ram_1_dout[0] : 1'bz;  // Controlled_Buffer controlled_buffer_1
  assign out_27 = rom_1_data[15] ? ram_1_dout[1] : 1'bz;  // Controlled_Buffer controlled_buffer_2
  assign out_26 = rom_1_data[15] ? ram_1_dout[2] : 1'bz;  // Controlled_Buffer controlled_buffer_3
  assign out_25 = rom_1_data[15] ? ram_1_dout[3] : 1'bz;  // Controlled_Buffer controlled_buffer_4
  assign out_24 = rom_1_data[15] ? ram_1_dout[4] : 1'bz;  // Controlled_Buffer controlled_buffer_5
  assign out_23 = rom_1_data[15] ? ram_1_dout[5] : 1'bz;  // Controlled_Buffer controlled_buffer_6
  assign out_22 = rom_1_data[15] ? ram_1_dout[6] : 1'bz;  // Controlled_Buffer controlled_buffer_7
  assign out_21 = rom_1_data[15] ? ram_1_dout[7] : 1'bz;  // Controlled_Buffer controlled_buffer_8
  assign controlled_buffer_9_out[0] = rom_1_data[15] ? ram_1_dout[8] : 1'bz;  // Controlled_Buffer controlled_buffer_9
  assign controlled_buffer_9_out[1] = rom_1_data[15] ? ram_1_dout[9] : 1'bz;  // Controlled_Buffer controlled_buffer_10
  assign controlled_buffer_9_out[2] = rom_1_data[15] ? ram_1_dout[10] : 1'bz;  // Controlled_Buffer controlled_buffer_11
  assign controlled_buffer_9_out[3] = rom_1_data[15] ? ram_1_dout[11] : 1'bz;  // Controlled_Buffer controlled_buffer_12
  assign controlled_buffer_9_out[4] = rom_1_data[15] ? ram_1_dout[12] : 1'bz;  // Controlled_Buffer controlled_buffer_13
  LED led_53 (.in(ram_1_dout[0]));
  LED led_54 (.in(d_ff_21_q));
  assign out_28 = rom_1_data[13] ? d_ff_21_q : 1'bz;  // Controlled_Buffer controlled_buffer_14
  assign out_27 = rom_1_data[13] ? d_ff_20_q : 1'bz;  // Controlled_Buffer controlled_buffer_15
  assign out_26 = rom_1_data[13] ? d_ff_15_q : 1'bz;  // Controlled_Buffer controlled_buffer_16
  assign out_25 = rom_1_data[13] ? d_ff_9_q : 1'bz;  // Controlled_Buffer controlled_buffer_17
  assign out_24 = rom_1_data[13] ? d_ff_4_q : 1'bz;  // Controlled_Buffer controlled_buffer_18
  assign out_23 = rom_1_data[13] ? d_ff_5_q : 1'bz;  // Controlled_Buffer controlled_buffer_19
  assign out_22 = rom_1_data[13] ? d_ff_10_q : 1'bz;  // Controlled_Buffer controlled_buffer_20
  assign out_21 = rom_1_data[13] ? d_ff_16_q : 1'bz;  // Controlled_Buffer controlled_buffer_21
  not not_3 (not_3_out, and_2_out);
  LED led_55 (.in(demultiplexer_1_out14));
  LED led_56 (.in(demultiplexer_1_out15));
  LED led_57 (.in(out_21));
  LED led_58 (.in(out_22));
  LED led_59 (.in(out_23));
  LED led_60 (.in(out_24));
  LED led_61 (.in(out_25));
  LED led_62 (.in(out_26));
  LED led_63 (.in(out_27));
  LED led_64 (.in(out_28));
  and and_4 (and_4_out, and_2_out, rom_1_data[12]);
  LED led_65 (.in(adder_1_cout));
  ROM rom_2 (.addr(d_ff_45_q), .data(rom_2_data));
  and and_5 (and_5_out, out_28, rom_1_data[10]);
  J_K_Flip_Flop j_k_ff_5 (
    .J(in_4), .K(in_4), .clk(and_4_out), .Q(j_k_ff_5_q), .Qn(j_k_ff_5_qn), .preset(and_5_out),
    .reset(multiplexer_11_out));
  assign out_21 = rom_1_data[11] ? j_k_ff_12_q : 1'bz;  // Controlled_Buffer controlled_buffer_22
  assign out_22 = rom_1_data[11] ? j_k_ff_11_q : 1'bz;  // Controlled_Buffer controlled_buffer_23
  assign out_23 = rom_1_data[11] ? j_k_ff_10_q : 1'bz;  // Controlled_Buffer controlled_buffer_24
  assign out_24 = rom_1_data[11] ? j_k_ff_9_q : 1'bz;  // Controlled_Buffer controlled_buffer_25
  assign out_25 = rom_1_data[11] ? j_k_ff_8_q : 1'bz;  // Controlled_Buffer controlled_buffer_26
  assign out_26 = rom_1_data[11] ? j_k_ff_7_q : 1'bz;  // Controlled_Buffer controlled_buffer_27
  assign out_27 = rom_1_data[11] ? j_k_ff_6_q : 1'bz;  // Controlled_Buffer controlled_buffer_28
  assign out_28 = rom_1_data[11] ? j_k_ff_5_q : 1'bz;  // Controlled_Buffer controlled_buffer_29
  D_Flip_Flop d_ff_22 (.D(out_21), .clk(and_13_out), .Q(d_ff_22_q), .preset(in_9), .reset(A_CLEAR));  // open: Qn
  assign out_21 = rom_1_data[8] ? d_ff_22_q : 1'bz;  // Controlled_Buffer controlled_buffer_30
  assign out_22 = rom_1_data[8] ? d_ff_25_q : 1'bz;  // Controlled_Buffer controlled_buffer_31
  assign out_23 = rom_1_data[8] ? d_ff_26_q : 1'bz;  // Controlled_Buffer controlled_buffer_32
  Adder #(.width(1)) adder_1 (.a(d_ff_22_q), .b(xor_1_out), .out(adder_1_out), .cin(adder_2_cout), .cout(adder_1_cout));
  xor xor_1 (xor_1_out, rom_1_data[7], d_ff_23_q);
  xor xor_2 (xor_2_out, rom_1_data[7], d_ff_27_q);
  assign out_21 = rom_1_data[6] ? adder_1_out : 1'bz;  // Controlled_Buffer controlled_buffer_33
  assign out_22 = rom_1_data[6] ? adder_2_out : 1'bz;  // Controlled_Buffer controlled_buffer_34
  assign out_23 = rom_1_data[6] ? adder_3_out : 1'bz;  // Controlled_Buffer controlled_buffer_35
  D_Flip_Flop d_ff_23 (.D(out_21), .clk(and_14_out), .Q(d_ff_23_q), .preset(in_13), .reset(B_CLEAR));  // open: Qn
  assign out_21 = rom_1_data[2] ? d_ff_23_q : 1'bz;  // Controlled_Buffer controlled_buffer_36
  assign out_22 = rom_1_data[2] ? d_ff_27_q : 1'bz;  // Controlled_Buffer controlled_buffer_37
  assign out_23 = rom_1_data[2] ? d_ff_28_q : 1'bz;  // Controlled_Buffer controlled_buffer_38
  D_Flip_Flop d_ff_24 (.D(out_21), .clk(and_15_out), .Q(d_ff_45_q[7]), .reset(O_CLEAR));  // open: Qn, preset
  and and_6 (and_6_out, out_27, rom_1_data[10]);
  J_K_Flip_Flop j_k_ff_6 (
    .J(in_4), .K(in_4), .clk(j_k_ff_5_qn), .Q(j_k_ff_6_q), .Qn(j_k_ff_6_qn), .preset(and_6_out),
    .reset(multiplexer_11_out));
  J_K_Flip_Flop j_k_ff_7 (
    .J(in_4), .K(in_4), .clk(j_k_ff_6_qn), .Q(j_k_ff_7_q), .Qn(j_k_ff_7_qn), .preset(and_7_out),
    .reset(multiplexer_11_out));
  LED led_66 (.in(j_k_ff_12_q));
  LED led_67 (.in(j_k_ff_11_q));
  D_Flip_Flop d_ff_25 (.D(out_22), .clk(and_13_out), .Q(d_ff_25_q), .preset(in_9), .reset(A_CLEAR));  // open: Qn
  D_Flip_Flop d_ff_26 (.D(out_23), .clk(and_13_out), .Q(d_ff_26_q), .preset(in_9), .reset(A_CLEAR));  // open: Qn
  LED led_68 (.in(d_ff_22_q));
  LED led_69 (.in(d_ff_25_q));
  assign out_24 = rom_1_data[8] ? d_ff_31_q : 1'bz;  // Controlled_Buffer controlled_buffer_39
  Adder #(.width(1)) adder_2 (.a(d_ff_25_q), .b(xor_2_out), .out(adder_2_out), .cin(adder_3_cout), .cout(adder_2_cout));
  xor xor_3 (xor_3_out, rom_1_data[7], d_ff_28_q);
  LED led_70 (.in(adder_1_out));
  LED led_71 (.in(adder_2_out));
  assign out_24 = rom_1_data[6] ? adder_4_out : 1'bz;  // Controlled_Buffer controlled_buffer_40
  D_Flip_Flop d_ff_27 (.D(out_22), .clk(and_14_out), .Q(d_ff_27_q), .preset(in_13), .reset(B_CLEAR));  // open: Qn
  D_Flip_Flop d_ff_28 (.D(out_23), .clk(and_14_out), .Q(d_ff_28_q), .preset(in_13), .reset(B_CLEAR));  // open: Qn
  LED led_72 (.in(d_ff_23_q));
  LED led_73 (.in(d_ff_27_q));
  assign out_24 = rom_1_data[2] ? d_ff_32_q : 1'bz;  // Controlled_Buffer controlled_buffer_41
  D_Flip_Flop d_ff_29 (.D(out_22), .clk(and_15_out), .Q(d_ff_45_q[6]), .reset(O_CLEAR));  // open: Qn, preset
  D_Flip_Flop d_ff_30 (.D(out_23), .clk(and_15_out), .Q(d_ff_45_q[5]), .reset(O_CLEAR));  // open: Qn, preset
  LED led_74 (.in(d_ff_45_q[7]));
  LED led_75 (.in(d_ff_45_q[6]));
  LED MI (.in(rom_1_data[16]));
  LED RO (.in(rom_1_data[15]));
  LED II (.in(rom_1_data[14]));
  and and_7 (and_7_out, out_26, rom_1_data[10]);
  J_K_Flip_Flop j_k_ff_8 (
    .J(in_4), .K(in_4), .clk(j_k_ff_7_qn), .Q(j_k_ff_8_q), .Qn(j_k_ff_8_qn), .preset(and_9_out),
    .reset(multiplexer_11_out));
  LED led_76 (.in(j_k_ff_10_q));
  LED led_77 (.in(j_k_ff_9_q));
  LED led_78 (.in(j_k_ff_8_q));
  LED led_79 (.in(j_k_ff_7_q));
  D_Flip_Flop d_ff_31 (.D(out_24), .clk(and_13_out), .Q(d_ff_31_q), .preset(in_9), .reset(A_CLEAR));  // open: Qn
  LED led_80 (.in(d_ff_26_q));
  LED led_81 (.in(d_ff_31_q));
  LED led_82 (.in(d_ff_34_q));
  LED led_83 (.in(d_ff_37_q));
  Adder #(.width(1)) adder_3 (.a(d_ff_26_q), .b(xor_3_out), .out(adder_3_out), .cin(adder_4_cout), .cout(adder_3_cout));
  Adder #(.width(1)) adder_4 (.a(d_ff_31_q), .b(xor_4_out), .out(adder_4_out), .cin(adder_6_cout), .cout(adder_4_cout));
  xor xor_4 (xor_4_out, rom_1_data[7], d_ff_32_q);
  xor xor_5 (xor_5_out, rom_1_data[7], d_ff_35_q);
  LED led_84 (.in(adder_3_out));
  LED led_85 (.in(adder_4_out));
  LED led_86 (.in(adder_6_out));
  LED led_87 (.in(adder_5_out));
  D_Flip_Flop d_ff_32 (.D(out_24), .clk(and_14_out), .Q(d_ff_32_q), .preset(in_13), .reset(B_CLEAR));  // open: Qn
  LED led_88 (.in(d_ff_28_q));
  LED led_89 (.in(d_ff_32_q));
  LED led_90 (.in(d_ff_35_q));
  LED led_91 (.in(d_ff_38_q));
  D_Flip_Flop d_ff_33 (.D(out_24), .clk(and_15_out), .Q(d_ff_45_q[4]), .reset(O_CLEAR));  // open: Qn, preset
  LED led_92 (.in(d_ff_45_q[5]));
  LED led_93 (.in(d_ff_45_q[4]));
  LED led_94 (.in(d_ff_45_q[3]));
  LED led_95 (.in(d_ff_45_q[2]));
  ROM rom_3 (.addr(d_ff_45_q), .data(rom_3_data));
  _7_Segment_Display u_7_segment_display_1 (
    .g(rom_2_data[1]), .f(rom_2_data[2]), .a(rom_2_data[7]), .b(rom_2_data[6]), .e(rom_2_data[3]),
    .d(rom_2_data[4]), .c(rom_2_data[5]));  // open: dp
  LED IO (.in(rom_1_data[13]));
  LED CE (.in(rom_1_data[12]));
  LED CO (.in(rom_1_data[11]));
  LED J (.in(rom_1_data[10]));
  and and_8 (and_8_out, out_24, rom_1_data[10]);
  and and_9 (and_9_out, out_25, rom_1_data[10]);
  J_K_Flip_Flop j_k_ff_9 (
    .J(in_4), .K(in_4), .clk(j_k_ff_8_qn), .Q(j_k_ff_9_q), .Qn(j_k_ff_9_qn), .preset(and_8_out),
    .reset(multiplexer_11_out));
  LED led_96 (.in(j_k_ff_6_q));
  LED led_97 (.in(j_k_ff_5_q));
  D_Flip_Flop d_ff_34 (.D(out_25), .clk(and_13_out), .Q(d_ff_34_q), .preset(in_9), .reset(A_CLEAR));  // open: Qn
  LED led_98 (.in(d_ff_40_q));
  LED led_99 (.in(d_ff_43_q));
  Adder #(.width(1)) adder_5 (.a(d_ff_37_q), .b(xor_6_out), .out(adder_5_out), .cin(adder_7_cout), .cout(adder_5_cout));
  Adder #(.width(1)) adder_6 (.a(d_ff_34_q), .b(xor_5_out), .out(adder_6_out), .cin(adder_5_cout), .cout(adder_6_cout));
  xor xor_6 (xor_6_out, rom_1_data[7], d_ff_38_q);
  LED led_100 (.in(adder_7_out));
  LED led_101 (.in(adder_8_out));
  D_Flip_Flop d_ff_35 (.D(out_25), .clk(and_14_out), .Q(d_ff_35_q), .preset(in_13), .reset(B_CLEAR));  // open: Qn
  LED led_102 (.in(d_ff_41_q));
  LED led_103 (.in(d_ff_44_q));
  D_Flip_Flop d_ff_36 (.D(out_25), .clk(and_15_out), .Q(d_ff_45_q[3]), .reset(O_CLEAR));  // open: Qn, preset
  LED led_104 (.in(d_ff_45_q[1]));
  LED led_105 (.in(d_ff_45_q[0]));
  _7_Segment_Display u_7_segment_display_2 (
    .g(rom_4_data[1]), .f(rom_4_data[2]), .a(rom_4_data[7]), .b(rom_4_data[6]), .e(rom_4_data[3]),
    .d(rom_4_data[4]), .c(rom_4_data[5]));  // open: dp
  _7_Segment_Display u_7_segment_display_3 (
    .g(rom_3_data[1]), .f(rom_3_data[2]), .a(rom_3_data[7]), .b(rom_3_data[6]), .e(rom_3_data[3]),
    .d(rom_3_data[4]), .c(rom_3_data[5]));  // open: dp
  LED SU (.in(rom_1_data[7]));
  LED SO (.in(rom_1_data[6]));
  LED AI (.in(rom_1_data[9]));
  LED AO (.in(rom_1_data[8]));
  and and_10 (and_10_out, out_23, rom_1_data[10]);
  J_K_Flip_Flop j_k_ff_10 (
    .J(in_4), .K(in_4), .clk(j_k_ff_9_qn), .Q(j_k_ff_10_q), .Qn(j_k_ff_10_qn), .preset(and_10_out),
    .reset(multiplexer_11_out));
  D_Flip_Flop d_ff_37 (.D(out_26), .clk(and_13_out), .Q(d_ff_37_q), .preset(in_9), .reset(A_CLEAR));  // open: Qn
  assign out_25 = rom_1_data[8] ? d_ff_34_q : 1'bz;  // Controlled_Buffer controlled_buffer_42
  assign out_26 = rom_1_data[8] ? d_ff_37_q : 1'bz;  // Controlled_Buffer controlled_buffer_43
  assign out_27 = rom_1_data[8] ? d_ff_40_q : 1'bz;  // Controlled_Buffer controlled_buffer_44
  assign out_28 = rom_1_data[8] ? d_ff_43_q : 1'bz;  // Controlled_Buffer controlled_buffer_45
  Adder #(.width(1)) adder_7 (.a(d_ff_40_q), .b(xor_7_out), .out(adder_7_out), .cin(adder_8_cout), .cout(adder_7_cout));
  xor xor_7 (xor_7_out, rom_1_data[7], d_ff_41_q);
  xor xor_8 (xor_8_out, rom_1_data[7], d_ff_44_q);
  assign out_25 = rom_1_data[6] ? adder_6_out : 1'bz;  // Controlled_Buffer controlled_buffer_46
  assign out_26 = rom_1_data[6] ? adder_5_out : 1'bz;  // Controlled_Buffer controlled_buffer_47
  D_Flip_Flop d_ff_38 (.D(out_26), .clk(and_14_out), .Q(d_ff_38_q), .preset(in_13), .reset(B_CLEAR));  // open: Qn
  assign out_25 = rom_1_data[2] ? d_ff_35_q : 1'bz;  // Controlled_Buffer controlled_buffer_48
  assign out_26 = rom_1_data[2] ? d_ff_38_q : 1'bz;  // Controlled_Buffer controlled_buffer_49
  D_Flip_Flop d_ff_39 (.D(out_26), .clk(and_15_out), .Q(d_ff_45_q[2]), .reset(O_CLEAR));  // open: Qn, preset
  LED OI (.in(rom_1_data[5]));
  LED HT (.in(rom_1_data[4]));
  LED BI (.in(rom_1_data[3]));
  LED BO (.in(rom_1_data[2]));
  and and_11 (and_11_out, out_22, rom_1_data[10]);
  J_K_Flip_Flop j_k_ff_11 (
    .J(in_4), .K(in_4), .clk(j_k_ff_10_qn), .Q(j_k_ff_11_q), .Qn(j_k_ff_11_qn), .preset(and_11_out),
    .reset(multiplexer_11_out));
  D_Flip_Flop d_ff_40 (.D(out_27), .clk(and_13_out), .Q(d_ff_40_q), .preset(in_9), .reset(A_CLEAR));  // open: Qn
  Adder #(.width(1)) adder_8 (
    .a(d_ff_43_q), .b(xor_8_out), .out(adder_8_out), .cin(rom_1_data[7]), .cout(adder_8_cout));
  assign out_27 = rom_1_data[6] ? adder_7_out : 1'bz;  // Controlled_Buffer controlled_buffer_50
  assign out_28 = rom_1_data[6] ? adder_8_out : 1'bz;  // Controlled_Buffer controlled_buffer_51
  D_Flip_Flop d_ff_41 (.D(out_27), .clk(and_14_out), .Q(d_ff_41_q), .preset(in_13), .reset(B_CLEAR));  // open: Qn
  assign out_27 = rom_1_data[2] ? d_ff_41_q : 1'bz;  // Controlled_Buffer controlled_buffer_52
  assign out_28 = rom_1_data[2] ? d_ff_44_q : 1'bz;  // Controlled_Buffer controlled_buffer_53
  D_Flip_Flop d_ff_42 (.D(out_27), .clk(and_15_out), .Q(d_ff_45_q[1]), .reset(O_CLEAR));  // open: Qn, preset
  ROM rom_4 (.addr(d_ff_45_q), .data(rom_4_data));
  LED RC (.in(rom_1_data[1]));
  LED CC (.in(rom_1_data[0]));
  and and_12 (and_12_out, out_21, rom_1_data[10]);
  J_K_Flip_Flop j_k_ff_12 (
    .J(in_4), .K(in_4), .clk(j_k_ff_11_qn), .Q(j_k_ff_12_q), .preset(and_12_out), .reset(multiplexer_11_out));  // open: Qn
  and and_13 (and_13_out, and_2_out, rom_1_data[9]);
  D_Flip_Flop d_ff_43 (.D(out_28), .clk(and_13_out), .Q(d_ff_43_q), .preset(in_9), .reset(A_CLEAR));  // open: Qn
  and and_14 (and_14_out, and_2_out, rom_1_data[3]);
  D_Flip_Flop d_ff_44 (.D(out_28), .clk(and_14_out), .Q(d_ff_44_q), .preset(in_13), .reset(B_CLEAR));  // open: Qn
  D_Flip_Flop d_ff_45 (.D(out_28), .clk(and_15_out), .Q(d_ff_45_q[0]), .reset(O_CLEAR));  // open: Qn, preset
  Multiplexer multiplexer_11 (.in0(rom_1_data[0]), .in1(button_1_out), .out(multiplexer_11_out), .sel(in_5));
  Button button_1 (.out(button_1_out));
  and and_15 (and_15_out, and_2_out, rom_1_data[5]);
  and and_16 (and_16_out, and_2_out, FI);
  D_Flip_Flop d_ff_46 (.D(adder_1_cout), .clk(and_16_out), .Q(d_ff_46_q), .preset(undriven_4), .reset(FR));  // open: Qn
  D_Flip_Flop d_ff_47 (.D(nor_1_out), .clk(and_16_out), .Q(d_ff_47_q), .preset(undriven_4), .reset(FR));  // open: Qn
  LED CF (.in(d_ff_46_q));
  LED ZF (.in(d_ff_47_q));
  nor nor_1 (nor_1_out, adder_1_out, adder_2_out, adder_3_out, adder_4_out, adder_6_out, adder_5_out, adder_7_out, adder_8_out);
  LED led_106 (.in(nor_1_out));

  // Notes on the sheet:
  //   MAR
  //   II
  //   CHA
  //   contents of rom_1 (hex, n*v repeats v):
  //   10800 0 d000 13*0 10800 0 d000 10 12*0 10800 0 d000 13*0 10800 0 d000 12000 0 8200 2 9*0 10800 0
  //   d000 1100 1 11*0 10800 0 d000 12000 0 8008 240 2 8*0 10800 0 d000 13*0 10800 0 d000 120 2 11*0 10800
  //   0 d000 13*0 10800 0 d000 13*0 10800 0 d000 13*0 10800 0 d000 13*0 10800 0 d000 13*0 10800 0 d000
  //   13*0 10800 0 d000 13*0 10800 0 d000 13*0 10800 0 d000 1 2400 2 10*0 10800 0 d000 13*0 10800 0 d000
  //   13*0 10800 0 d000 13*0 10800 0 d000 13*0 10800 0 d000 13*0 10800 0 d000 13*0 10800 0 d000 13*0 10800
  //   0 d000 13*0 10800 0 d000 13*0 10800 0 d000 13*0 10800 0 d000 13*0 10800 0 d000 13*0 10800 0 d000
  //   13*0 10800 0 d000 13*0 10800 0 d000
  //   RAM DATA INPUT
  //   INSTRUCTION REGISTER
  //   STEP COUNTER
  //           INPUT ADDRESS
  //   MI
  //   RO
  //   RAM DATA
  //   IO
  //       8 BIT BUS
  //   contents of rom_2 (hex, n*v repeats v):
  //   100*fc 100*60 56*da
  //   PROGRAM COUNTER
  //          A REGISTER
  //         ALU
  //               B REGISTER
  //   OUTPUT_REGISTER
  //   contents of rom_3 (hex, n*v repeats v):
  //   10*fc 10*60 10*da 10*f2 10*66 10*b6 10*be 10*e0 10*fe 10*f6 10*fc 10*60 10*da 10*f2 10*66 10*b6
  //   10*be 10*e0 10*fe 10*f6 10*fc 10*60 10*da 10*f2 10*66 6*b6
  //   OUTPUT_DISPLAY
  //   CONTROL_WORD
  //   contents of rom_4 (hex, n*v repeats v):
  //   fc 60 da f2 66 b6 be e0 fe f6 fc 60 da f2 66 b6 be e0 fe f6 fc 60 da f2 66 b6 be e0 fe f6 fc 60 da
  //   f2 66 b6 be e0 fe f6 fc 60 da f2 66 b6 be e0 fe f6 fc 60 da f2 66 b6 be e0 fe f6 fc 60 da f2 66 b6
  //   be e0 fe f6 fc 60 da f2 66 b6 be e0 fe f6 fc 60 da f2 66 b6 be e0 fe f6 fc 60 da f2 66 b6 be e0 fe
  //   f6 fc 60 da f2 66 b6 be e0 fe f6 fc 60 da f2 66 b6 be e0 fe f6 fc 60 da f2 66 b6 be e0 fe f6 fc 60
  //   da f2 66 b6 be e0 fe f6 fc 60 da f2 66 b6 be e0 fe f6 fc 60 da f2 66 b6 be e0 fe f6 fc 60 da f2 66
  //   b6 be e0 fe f6 fc 60 da f2 66 b6 be e0 fe f6 fc 60 da f2 66 b6 be e0 fe f6 fc 60 da f2 66 b6 be e0
  //   fe f6 fc 60 da f2 66 b6 be e0 fe f6 fc 60 da f2 66 b6 be e0 fe f6 fc 60 da f2 66 b6 be e0 fe f6 fc
  //   60 da f2 66 b6 be e0 fe f6 fc 60 da f2 66 b6 be e0 fe f6 fc 60 da f2 66 b6
  //   SUB
  //   SO
  //   BO
  //   AI
  //   AO
  //   BI
  //   OI
  //   FLAGS_REGISTER
endmodule
